// Logisim project Chess Digital Timer Kelompok 7.circ as structural Verilog: 8 circuits, main circuit Chess Digital Clock
module Chess_Digital_Clock (
  input  _0_STOP___1_START,
  input  surrender,
  input  surrender_2,
  input  _0_MAGNUS___1_GAMMA
);

  wire Back_To_0_out, clock_1_out, GAMMA_kondisi_stop_timer, GAMMA_out_4, GAMMA_out_5, GAMMA_out_6,
       GAMMA_out_7, GAMMA_out_8, GAMMA_out_9, GAMMA_out_10, GAMMA_out_11, GAMMA_out_12, GAMMA_out_13,
       GAMMA_out_14, GAMMA_out_15, GAMMA_out_16, GAMMA_out_17, GAMMA_out_18, GAMMA_out_19, GAMMA_out_20,
       GAMMA_out_21, GAMMA_out_22, GAMMA_out_23, GAMMA_out_24, GAMMA_out_25, GAMMA_out_26, GAMMA_out_27,
       GAMMA_out_28, GAMMA_out_29, GAMMA_out_30, GAMMA_out_31, GAMMA_timer_menyentuh_0,
       MAGNUS_kondisi_stop_timer, MAGNUS_out_4, MAGNUS_out_5, MAGNUS_out_6, MAGNUS_out_7, MAGNUS_out_8,
       MAGNUS_out_9, MAGNUS_out_10, MAGNUS_out_11, MAGNUS_out_12, MAGNUS_out_13, MAGNUS_out_14,
       MAGNUS_out_15, MAGNUS_out_16, MAGNUS_out_17, MAGNUS_out_18, MAGNUS_out_19, MAGNUS_out_20,
       MAGNUS_out_21, MAGNUS_out_22, MAGNUS_out_23, MAGNUS_out_24, MAGNUS_out_25, MAGNUS_out_26,
       MAGNUS_out_27, MAGNUS_out_28, MAGNUS_out_29, MAGNUS_out_30, MAGNUS_out_31, MAGNUS_timer_menyentuh_0,
       not_1_out, or_1_out, or_2_out, or_3_out, START_TIMER_out, transistor_1_out, transistor_2_out,
       transistor_3_out;

  LED led_1 (.in(or_1_out));
  or or_1 (or_1_out, surrender, GAMMA_timer_menyentuh_0);
  LED led_2 (.in(or_3_out));
  _7_Segment_Display u_7_segment_display_1 (
    .g(GAMMA_out_9), .f(GAMMA_out_11), .a(GAMMA_out_17), .b(GAMMA_out_16), .e(GAMMA_out_13),
    .d(GAMMA_out_14), .c(GAMMA_out_15), .dp(transistor_1_out));
  _7_Segment_Display u_7_segment_display_2 (
    .g(GAMMA_out_20), .f(GAMMA_out_22), .a(GAMMA_out_31), .b(GAMMA_out_30), .e(GAMMA_out_24),
    .d(GAMMA_out_26), .c(GAMMA_out_28));  // open: dp
  _7_Segment_Display u_7_segment_display_3 (
    .g(GAMMA_out_18), .f(GAMMA_out_19), .a(GAMMA_out_29), .b(GAMMA_out_27), .e(GAMMA_out_21),
    .d(GAMMA_out_23), .c(GAMMA_out_25));  // open: dp
  or or_2 (or_2_out, MAGNUS_kondisi_stop_timer, ~_0_STOP___1_START, surrender_2, surrender, GAMMA_kondisi_stop_timer);  // OR_Gate
  not not_1 (not_1_out, _0_MAGNUS___1_GAMMA);
  Transistor transistor_1 (.in(transistor_2_out), .out(transistor_1_out), .gate(not_1_out));
  MM_SS GAMMA (
    .out_4(GAMMA_out_4), .out_5(GAMMA_out_5), .out_6(GAMMA_out_6), .out_7(GAMMA_out_7), .out_8(GAMMA_out_8),
    .out_10(GAMMA_out_10), .out_12(GAMMA_out_12), .out_18(GAMMA_out_18), .out_19(GAMMA_out_19),
    .out_21(GAMMA_out_21), .out_23(GAMMA_out_23), .out_25(GAMMA_out_25), .out_27(GAMMA_out_27),
    .out_29(GAMMA_out_29), .Clock(transistor_1_out), .out_9(GAMMA_out_9), .out_11(GAMMA_out_11),
    .out_13(GAMMA_out_13), .out_14(GAMMA_out_14), .out_15(GAMMA_out_15), .out_16(GAMMA_out_16),
    .out_17(GAMMA_out_17), .out_20(GAMMA_out_20), .out_22(GAMMA_out_22), .out_24(GAMMA_out_24),
    .out_26(GAMMA_out_26), .out_28(GAMMA_out_28), .out_30(GAMMA_out_30), .out_31(GAMMA_out_31),
    .Kondisi_Stop_Timer(GAMMA_kondisi_stop_timer), .Start_Condition(START_TIMER_out),
    .Back_To_0(Back_To_0_out), .Timer_Menyentuh_0(GAMMA_timer_menyentuh_0));
  _7_Segment_Display u_7_segment_display_4 (
    .g(GAMMA_out_4), .f(GAMMA_out_5), .a(GAMMA_out_12), .b(GAMMA_out_10), .e(GAMMA_out_6), .d(GAMMA_out_7),
    .c(GAMMA_out_8));  // open: dp
  Clock clock_1 (.out(clock_1_out));
  Transistor transistor_2 (.in(clock_1_out), .out(transistor_2_out), .gate(or_2_out));
  Button START_TIMER (.out(START_TIMER_out));
  Button Back_To_0 (.out(Back_To_0_out));
  _7_Segment_Display u_7_segment_display_5 (
    .g(MAGNUS_out_20), .f(MAGNUS_out_22), .a(MAGNUS_out_31), .b(MAGNUS_out_30), .e(MAGNUS_out_24),
    .d(MAGNUS_out_26), .c(MAGNUS_out_28));  // open: dp
  _7_Segment_Display u_7_segment_display_6 (
    .g(MAGNUS_out_9), .f(MAGNUS_out_11), .a(MAGNUS_out_17), .b(MAGNUS_out_16), .e(MAGNUS_out_13),
    .d(MAGNUS_out_14), .c(MAGNUS_out_15), .dp(transistor_3_out));
  _7_Segment_Display u_7_segment_display_7 (
    .g(MAGNUS_out_18), .f(MAGNUS_out_19), .a(MAGNUS_out_29), .b(MAGNUS_out_27), .e(MAGNUS_out_21),
    .d(MAGNUS_out_23), .c(MAGNUS_out_25));  // open: dp
  or or_3 (or_3_out, MAGNUS_timer_menyentuh_0, surrender_2);
  _7_Segment_Display u_7_segment_display_8 (
    .g(MAGNUS_out_4), .f(MAGNUS_out_5), .a(MAGNUS_out_12), .b(MAGNUS_out_10), .e(MAGNUS_out_6),
    .d(MAGNUS_out_7), .c(MAGNUS_out_8));  // open: dp
  Transistor transistor_3 (.in(transistor_2_out), .out(transistor_3_out), .gate(_0_MAGNUS___1_GAMMA));
  LED led_3 (.in(or_3_out));
  LED led_4 (.in(or_1_out));
  MM_SS MAGNUS (
    .out_4(MAGNUS_out_4), .out_5(MAGNUS_out_5), .out_6(MAGNUS_out_6), .out_7(MAGNUS_out_7),
    .out_8(MAGNUS_out_8), .out_10(MAGNUS_out_10), .out_12(MAGNUS_out_12), .out_18(MAGNUS_out_18),
    .out_19(MAGNUS_out_19), .out_21(MAGNUS_out_21), .out_23(MAGNUS_out_23), .out_25(MAGNUS_out_25),
    .out_27(MAGNUS_out_27), .out_29(MAGNUS_out_29), .Clock(transistor_3_out), .out_9(MAGNUS_out_9),
    .out_11(MAGNUS_out_11), .out_13(MAGNUS_out_13), .out_14(MAGNUS_out_14), .out_15(MAGNUS_out_15),
    .out_16(MAGNUS_out_16), .out_17(MAGNUS_out_17), .out_20(MAGNUS_out_20), .out_22(MAGNUS_out_22),
    .out_24(MAGNUS_out_24), .out_26(MAGNUS_out_26), .out_28(MAGNUS_out_28), .out_30(MAGNUS_out_30),
    .out_31(MAGNUS_out_31), .Kondisi_Stop_Timer(MAGNUS_kondisi_stop_timer),
    .Start_Condition(START_TIMER_out), .Back_To_0(Back_To_0_out), .Timer_Menyentuh_0(MAGNUS_timer_menyentuh_0));
endmodule

// (xx:xx)
module MM_SS (
  input  Clock,
  input  Back_To_0,
  input  Start_Condition,
  output out_4,
  output out_5,
  output out_6,
  output out_7,
  output out_8,
  output out_9,
  output out_10,
  output out_11,
  output out_12,
  output out_13,
  output out_14,
  output out_15,
  output out_16,
  output out_17,
  output out_18,
  output out_19,
  output out_20,
  output out_21,
  output out_22,
  output out_23,
  output out_24,
  output out_25,
  output out_26,
  output out_27,
  output out_28,
  output out_29,
  output out_30,
  output out_31,
  output Kondisi_Stop_Timer,
  output Timer_Menyentuh_0
);

  wire and_1_out, and_3_out, and_4_out, and_5_out, and_6_out, and_8_out, and_9_out, transistor_1_out;
  wire [3:0] counter_1_q, counter_2_q, counter_3_q, counter_4_q;

  Counter #(.width(4), .max('h9)) counter_1 (
    .load(1'b1), .Q(counter_1_q), .clk(transistor_1_out), .clr(Back_To_0));  // open: D, count, carry
  Transistor transistor_1 (.in(Clock), .out(transistor_1_out), .gate(Kondisi_Stop_Timer));
  Counter #(.width(4), .max('h5)) counter_2 (
    .load(1'b1), .Q(counter_2_q), .clk(and_1_out), .clr(Back_To_0));  // open: D, count, carry
  and and_1 (and_1_out, counter_1_q[3], counter_1_q[0], ~counter_1_q[2], ~counter_1_q[1]);  // AND_Gate
  and and_2 (Kondisi_Stop_Timer, ~Start_Condition, Timer_Menyentuh_0);  // AND_Gate
  S__7_segDisplay s_7_segdisplay_1 (
    .s03(counter_1_q[3]), .s02(counter_1_q[2]), .s01(counter_1_q[1]), .s00(counter_1_q[0]), .g(out_4),
    .f(out_5), .e(out_6), .d(out_7), .c(out_8), .b(out_10), .a(out_12));
  S__7_segDisplay_2 s_7_segdisplay_2 (
    .s02(counter_2_q[2]), .s01(counter_2_q[1]), .s00(counter_2_q[0]), .g(out_18), .f(out_19), .e(out_21),
    .d(out_23), .c(out_25), .b(out_27), .a(out_29));
  and and_3 (and_3_out, ~counter_1_q[0], ~counter_1_q[1], ~counter_1_q[2], ~counter_1_q[3]);  // AND_Gate
  and and_4 (and_4_out, ~counter_2_q[0], ~counter_2_q[1], ~counter_2_q[2], ~counter_2_q[3]);  // AND_Gate
  and and_5 (and_5_out, ~counter_2_q[3], counter_2_q[2], ~counter_2_q[1], counter_2_q[0]);  // AND_Gate
  Counter #(.width(4), .max('h9)) counter_3 (
    .load(1'b1), .Q(counter_3_q), .clk(and_5_out), .clr(Back_To_0));  // open: D, count, carry
  and and_6 (and_6_out, ~counter_3_q[0], ~counter_3_q[1], ~counter_3_q[2], ~counter_3_q[3]);  // AND_Gate
  Counter #(.width(4), .max('h2)) counter_4 (
    .load(1'b1), .Q(counter_4_q), .clk(and_8_out), .clr(Back_To_0));  // open: D, count, carry
  and and_7 (Timer_Menyentuh_0, and_4_out, and_3_out, and_6_out, and_9_out);
  and and_8 (and_8_out, counter_3_q[0], ~counter_3_q[1], ~counter_3_q[2], counter_3_q[3]);  // AND_Gate
  and and_9 (and_9_out, ~counter_4_q[0], ~counter_4_q[1], ~counter_4_q[2], ~counter_4_q[3]);  // AND_Gate
  M____7_segDisplay m_7_segdisplay_1 (
    .s03(counter_3_q[3]), .s02(counter_3_q[2]), .s01(counter_3_q[1]), .s00(counter_3_q[0]), .g(out_9),
    .f(out_11), .e(out_13), .d(out_14), .c(out_15), .b(out_16), .a(out_17));
  M_____7_segDisplay m_7_segdisplay_2 (
    .s01(counter_4_q[1]), .s00(counter_4_q[0]), .g(out_20), .f(out_22), .e(out_24), .d(out_26), .c(out_28),
    .b(out_30), .a(out_31));
endmodule

// --:-x
module S__7_segDisplay (
  input  s03,
  input  s02,
  input  s01,
  input  s00,
  output g,
  output f,
  output e,
  output d,
  output c,
  output b,
  output a
);

  wire and_1_out, and_2_out, and_3_out, and_4_out, and_5_out, and_6_out, and_7_out, and_8_out, and_9_out,
       and_10_out, and_11_out, and_12_out, and_13_out, and_14_out, and_15_out, and_16_out, and_17_out,
       and_18_out, and_19_out, and_20_out, and_21_out, and_22_out, and_23_out, and_24_out, and_25_out,
       and_26_out, and_27_out, not_1_out, not_2_out, not_3_out, not_4_out, not_5_out, not_6_out, not_7_out,
       not_8_out, not_9_out, not_10_out, not_11_out, not_12_out, not_13_out, not_14_out, not_15_out,
       not_16_out, not_17_out, not_18_out, not_19_out, not_20_out, not_21_out, not_22_out, not_23_out,
       not_24_out, not_25_out, not_26_out, not_27_out, not_28_out, not_29_out, not_30_out, not_31_out,
       not_32_out, not_33_out, not_34_out, not_35_out, not_36_out, not_37_out, not_38_out, not_39_out,
       not_40_out, not_41_out, not_42_out;

  not not_1 (not_1_out, s03);
  and and_1 (and_1_out, not_1_out, not_2_out, s01);
  not not_2 (not_2_out, s02);
  and and_2 (and_2_out, s01, not_3_out);
  not not_3 (not_3_out, s00);
  and and_3 (and_3_out, s02, not_4_out);
  not not_4 (not_4_out, s01);
  and and_4 (and_4_out, s03, not_5_out);
  not not_5 (not_5_out, s01);
  and and_5 (and_5_out, s03, s02);
  not not_6 (not_6_out, s03);
  and and_6 (and_6_out, not_6_out, not_7_out, not_8_out);
  not not_7 (not_7_out, s01);
  not not_8 (not_8_out, s00);
  not not_9 (not_9_out, s03);
  and and_7 (and_7_out, not_9_out, s02, not_10_out);
  not not_10 (not_10_out, s01);
  not not_11 (not_11_out, s03);
  and and_8 (and_8_out, not_11_out, s02, not_12_out);
  not not_12 (not_12_out, s00);
  not not_13 (not_13_out, s02);
  and and_9 (and_9_out, s03, not_13_out, not_14_out);
  not not_14 (not_14_out, s01);
  not not_15 (not_15_out, s02);
  and and_10 (and_10_out, not_15_out, not_16_out);
  not not_16 (not_16_out, s00);
  not not_17 (not_17_out, s03);
  and and_11 (and_11_out, not_17_out, s01, not_18_out);
  not not_18 (not_18_out, s00);
  and and_12 (and_12_out, s03, not_19_out, not_20_out);
  not not_19 (not_19_out, s01);
  not not_20 (not_20_out, s00);
  not not_21 (not_21_out, s02);
  and and_13 (and_13_out, not_21_out, not_22_out);
  not not_22 (not_22_out, s00);
  not not_23 (not_23_out, s03);
  not not_24 (not_24_out, s02);
  and and_14 (and_14_out, not_23_out, not_24_out, s01);
  not not_25 (not_25_out, s03);
  and and_15 (and_15_out, not_25_out, s01, not_26_out);
  not not_26 (not_26_out, s00);
  and and_16 (and_16_out, s02, not_27_out, s00);
  not not_27 (not_27_out, s01);
  not not_28 (not_28_out, s02);
  and and_17 (and_17_out, s03, not_28_out, not_29_out);
  not not_29 (not_29_out, s01);
  and and_18 (and_18_out, s03, s02, s00);
  not not_30 (not_30_out, s02);
  and and_19 (and_19_out, not_30_out, not_31_out);
  not not_31 (not_31_out, s01);
  not not_32 (not_32_out, s03);
  and and_20 (and_20_out, not_32_out, s02);
  not not_33 (not_33_out, s03);
  and and_21 (and_21_out, not_33_out, not_34_out, not_35_out);
  not not_34 (not_34_out, s01);
  not not_35 (not_35_out, s00);
  not not_36 (not_36_out, s02);
  and and_22 (and_22_out, s01, s00);
  and and_23 (and_23_out, s03, s01);
  not not_37 (not_37_out, s02);
  and and_24 (and_24_out, not_37_out, not_38_out);
  not not_38 (not_38_out, s00);
  not not_39 (not_39_out, s03);
  and and_25 (and_25_out, not_39_out, s01);
  not not_40 (not_40_out, s03);
  and and_26 (and_26_out, not_40_out, s02, s00);
  not not_41 (not_41_out, s02);
  and and_27 (and_27_out, s03, not_41_out, not_42_out);
  not not_42 (not_42_out, s01);
  or or_1 (g, and_1_out, and_2_out, and_3_out, and_4_out, and_5_out);
  or or_2 (f, and_6_out, and_7_out, and_8_out, and_9_out);
  or or_3 (e, and_10_out, and_11_out, and_12_out);
  or or_4 (c, and_19_out, s00, and_20_out);
  or or_5 (b, and_21_out, not_36_out, and_22_out, and_23_out);
  or or_6 (a, and_24_out, and_25_out, and_26_out, and_27_out);
  or or_7 (d, and_13_out, and_14_out, and_15_out, and_16_out, and_17_out, and_18_out);
endmodule

// --:x-
module S__7_segDisplay_2 (
  input  s02,
  input  s01,
  input  s00,
  output g,
  output f,
  output e,
  output d,
  output c,
  output b,
  output a
);

  wire and_1_out, and_2_out, and_4_out, and_5_out, and_6_out, and_7_out, and_8_out, and_9_out, not_1_out,
       not_2_out, not_3_out, not_4_out, not_5_out, not_6_out, not_7_out, not_8_out, not_9_out, not_10_out,
       not_11_out, not_12_out, not_13_out, not_14_out, not_15_out, not_16_out;

  or or_1 (g, s01, s02);
  not not_1 (not_1_out, s01);
  not not_2 (not_2_out, s00);
  not not_3 (not_3_out, s01);
  not not_4 (not_4_out, s02);
  not not_5 (not_5_out, s00);
  not not_6 (not_6_out, s02);
  not not_7 (not_7_out, s00);
  not not_8 (not_8_out, s02);
  not not_9 (not_9_out, s01);
  not not_10 (not_10_out, s01);
  not not_11 (not_11_out, s02);
  not not_12 (not_12_out, s00);
  not not_13 (not_13_out, s02);
  not not_14 (not_14_out, s00);
  not not_15 (not_15_out, s02);
  not not_16 (not_16_out, s01);
  and and_1 (and_1_out, not_1_out, not_2_out);
  and and_2 (and_2_out, s02, not_3_out);
  and and_3 (e, not_4_out, not_5_out);
  and and_4 (and_4_out, not_6_out, not_7_out);
  and and_5 (and_5_out, not_8_out, s01);
  and and_6 (and_6_out, s02, not_9_out, s00);
  or or_2 (c, not_10_out, s00);
  or or_3 (b, not_11_out, not_12_out, s01);
  and and_7 (and_7_out, not_13_out, not_14_out);
  and and_8 (and_8_out, not_15_out, s01);
  and and_9 (and_9_out, s02, not_16_out, s00);
  or or_4 (f, and_1_out, and_2_out);
  or or_5 (d, and_4_out, and_5_out, and_6_out);
  or or_6 (a, and_7_out, and_8_out, and_9_out);
endmodule

// -x:--
module M____7_segDisplay (
  input  s03,
  input  s02,
  input  s01,
  input  s00,
  output g,
  output f,
  output e,
  output d,
  output c,
  output b,
  output a
);

  wire and_1_out, and_2_out, and_3_out, and_4_out, and_5_out, and_6_out, and_7_out, and_8_out, and_9_out,
       and_10_out, and_11_out, and_12_out, and_13_out, and_14_out, and_15_out, and_16_out, and_17_out,
       and_18_out, and_19_out, and_20_out, and_21_out, and_22_out, and_23_out, and_24_out, and_25_out,
       and_26_out, and_27_out, not_1_out, not_2_out, not_3_out, not_4_out, not_5_out, not_6_out, not_7_out,
       not_8_out, not_9_out, not_10_out, not_11_out, not_12_out, not_13_out, not_14_out, not_15_out,
       not_16_out, not_17_out, not_18_out, not_19_out, not_20_out, not_21_out, not_22_out, not_23_out,
       not_24_out, not_25_out, not_26_out, not_27_out, not_28_out, not_29_out, not_30_out, not_31_out,
       not_32_out, not_33_out, not_34_out, not_35_out, not_36_out, not_37_out, not_38_out, not_39_out,
       not_40_out, not_41_out, not_42_out;

  not not_1 (not_1_out, s03);
  and and_1 (and_1_out, not_1_out, not_2_out, s01);
  not not_2 (not_2_out, s02);
  and and_2 (and_2_out, s01, not_3_out);
  not not_3 (not_3_out, s00);
  and and_3 (and_3_out, s02, not_4_out);
  not not_4 (not_4_out, s01);
  and and_4 (and_4_out, s03, not_5_out);
  not not_5 (not_5_out, s01);
  and and_5 (and_5_out, s03, s02);
  not not_6 (not_6_out, s03);
  not not_7 (not_7_out, s01);
  and and_6 (and_6_out, not_6_out, not_7_out, not_8_out);
  not not_8 (not_8_out, s00);
  not not_9 (not_9_out, s03);
  and and_7 (and_7_out, not_9_out, s02, not_10_out);
  not not_10 (not_10_out, s01);
  not not_11 (not_11_out, s03);
  and and_8 (and_8_out, not_11_out, s02, not_12_out);
  not not_12 (not_12_out, s00);
  not not_13 (not_13_out, s02);
  and and_9 (and_9_out, s03, not_13_out, not_14_out);
  not not_14 (not_14_out, s01);
  not not_15 (not_15_out, s02);
  and and_10 (and_10_out, not_15_out, not_16_out);
  not not_16 (not_16_out, s00);
  not not_17 (not_17_out, s03);
  and and_11 (and_11_out, not_17_out, s01, not_18_out);
  not not_18 (not_18_out, s00);
  not not_19 (not_19_out, s01);
  and and_12 (and_12_out, s03, not_19_out, not_20_out);
  not not_20 (not_20_out, s00);
  not not_21 (not_21_out, s02);
  and and_13 (and_13_out, not_21_out, not_22_out);
  not not_22 (not_22_out, s00);
  not not_23 (not_23_out, s03);
  and and_14 (and_14_out, not_23_out, not_24_out, s01);
  not not_24 (not_24_out, s02);
  not not_25 (not_25_out, s03);
  and and_15 (and_15_out, not_25_out, s01, not_26_out);
  not not_26 (not_26_out, s00);
  and and_16 (and_16_out, s02, not_27_out, s00);
  not not_27 (not_27_out, s01);
  not not_28 (not_28_out, s02);
  and and_17 (and_17_out, s03, not_28_out, not_29_out);
  not not_29 (not_29_out, s01);
  and and_18 (and_18_out, s03, s02, s00);
  not not_30 (not_30_out, s02);
  and and_19 (and_19_out, not_30_out, not_31_out);
  not not_31 (not_31_out, s01);
  not not_32 (not_32_out, s03);
  and and_20 (and_20_out, not_32_out, s02);
  not not_33 (not_33_out, s03);
  not not_34 (not_34_out, s01);
  and and_21 (and_21_out, not_33_out, not_34_out, not_35_out);
  not not_35 (not_35_out, s00);
  not not_36 (not_36_out, s02);
  and and_22 (and_22_out, s01, s00);
  and and_23 (and_23_out, s03, s01);
  not not_37 (not_37_out, s02);
  and and_24 (and_24_out, not_37_out, not_38_out);
  not not_38 (not_38_out, s00);
  not not_39 (not_39_out, s03);
  and and_25 (and_25_out, not_39_out, s01);
  not not_40 (not_40_out, s03);
  and and_26 (and_26_out, not_40_out, s02, s00);
  and and_27 (and_27_out, s03, not_41_out, not_42_out);
  not not_41 (not_41_out, s02);
  not not_42 (not_42_out, s01);
  or or_1 (g, and_1_out, and_2_out, and_3_out, and_4_out, and_5_out);
  or or_2 (f, and_6_out, and_7_out, and_8_out, and_9_out);
  or or_3 (e, and_10_out, and_11_out, and_12_out);
  or or_4 (c, and_19_out, s00, and_20_out);
  or or_5 (b, and_21_out, not_36_out, and_22_out, and_23_out);
  or or_6 (a, and_24_out, and_25_out, and_26_out, and_27_out);
  or or_7 (d, and_13_out, and_14_out, and_15_out, and_16_out, and_17_out, and_18_out);
endmodule

// x-:--
module M_____7_segDisplay (
  input  s01,
  input  s00,
  output g,
  output f,
  output e,
  output d,
  output c,
  output b,
  output a
);

  wire and_2_out, and_3_out, not_1_out, not_2_out, not_3_out, not_4_out, not_5_out, not_6_out, not_7_out;

  not not_1 (not_1_out, s00);
  not not_2 (not_2_out, s01);
  not not_3 (not_3_out, s00);
  not not_4 (not_4_out, s00);
  not not_5 (not_5_out, s00);
  not not_6 (not_6_out, s01);
  not not_7 (not_7_out, s00);
  and and_1 (g, s01, not_1_out);
  and and_2 (and_2_out, not_2_out, not_3_out);
  and and_3 (and_3_out, s01, s00);
  or or_1 (e, not_4_out, s01);
  or or_2 (d, not_5_out, s01);
  or or_3 (c, not_6_out, s00);
  or or_4 (a, not_7_out, s01);
  or or_5 (f, and_2_out, and_3_out);

  assign b = 1'b1;
endmodule

module Implementasi_Sub_Circ (
);

  wire clock_1_out, clock_2_out, clock_3_out, clock_4_out, m_7_segdisplay_1_a, m_7_segdisplay_1_b,
       m_7_segdisplay_1_c, m_7_segdisplay_1_d, m_7_segdisplay_1_e, m_7_segdisplay_1_f, m_7_segdisplay_1_g,
       m_7_segdisplay_2_a, m_7_segdisplay_2_b, m_7_segdisplay_2_c, m_7_segdisplay_2_d, m_7_segdisplay_2_e,
       m_7_segdisplay_2_f, m_7_segdisplay_2_g, s_7_segdisplay_1_a, s_7_segdisplay_1_b, s_7_segdisplay_1_c,
       s_7_segdisplay_1_d, s_7_segdisplay_1_e, s_7_segdisplay_1_f, s_7_segdisplay_1_g, s_7_segdisplay_2_a,
       s_7_segdisplay_2_b, s_7_segdisplay_2_c, s_7_segdisplay_2_d, s_7_segdisplay_2_e, s_7_segdisplay_2_f,
       s_7_segdisplay_2_g;
  wire [3:0] counter_1_q, counter_2_q, counter_3_q, counter_4_q;

  Clock clock_1 (.out(clock_1_out));
  Clock clock_2 (.out(clock_2_out));
  Counter #(.width(4), .max('h9)) counter_1 (
    .load(1'b1), .Q(counter_1_q), .clk(clock_1_out));  // open: D, count, carry, clr
  Counter #(.width(4), .max('h5)) counter_2 (
    .load(1'b1), .Q(counter_2_q), .clk(clock_2_out));  // open: D, count, carry, clr
  S__7_segDisplay s_7_segdisplay_1 (
    .s03(counter_1_q[3]), .s02(counter_1_q[2]), .s01(counter_1_q[1]), .s00(counter_1_q[0]),
    .g(s_7_segdisplay_1_g), .f(s_7_segdisplay_1_f), .e(s_7_segdisplay_1_e), .d(s_7_segdisplay_1_d),
    .c(s_7_segdisplay_1_c), .b(s_7_segdisplay_1_b), .a(s_7_segdisplay_1_a));
  S__7_segDisplay_2 s_7_segdisplay_2 (
    .s02(counter_2_q[2]), .s01(counter_2_q[1]), .s00(counter_2_q[0]), .g(s_7_segdisplay_2_g),
    .f(s_7_segdisplay_2_f), .e(s_7_segdisplay_2_e), .d(s_7_segdisplay_2_d), .c(s_7_segdisplay_2_c),
    .b(s_7_segdisplay_2_b), .a(s_7_segdisplay_2_a));
  _7_Segment_Display u_7_segment_display_1 (
    .g(s_7_segdisplay_1_g), .f(s_7_segdisplay_1_f), .a(s_7_segdisplay_1_a), .b(s_7_segdisplay_1_b),
    .e(s_7_segdisplay_1_e), .d(s_7_segdisplay_1_d), .c(s_7_segdisplay_1_c));  // open: dp
  _7_Segment_Display u_7_segment_display_2 (
    .g(s_7_segdisplay_2_g), .f(s_7_segdisplay_2_f), .a(s_7_segdisplay_2_a), .b(s_7_segdisplay_2_b),
    .e(s_7_segdisplay_2_e), .d(s_7_segdisplay_2_d), .c(s_7_segdisplay_2_c));  // open: dp
  Clock clock_3 (.out(clock_3_out));
  Clock clock_4 (.out(clock_4_out));
  Counter #(.width(4), .max('h9)) counter_3 (
    .load(1'b1), .Q(counter_3_q), .clk(clock_3_out));  // open: D, count, carry, clr
  Counter #(.width(4), .max('h2)) counter_4 (
    .load(1'b1), .Q(counter_4_q), .clk(clock_4_out));  // open: D, count, carry, clr
  M____7_segDisplay m_7_segdisplay_1 (
    .s03(counter_3_q[3]), .s02(counter_3_q[2]), .s01(counter_3_q[1]), .s00(counter_3_q[0]),
    .g(m_7_segdisplay_1_g), .f(m_7_segdisplay_1_f), .e(m_7_segdisplay_1_e), .d(m_7_segdisplay_1_d),
    .c(m_7_segdisplay_1_c), .b(m_7_segdisplay_1_b), .a(m_7_segdisplay_1_a));
  M_____7_segDisplay m_7_segdisplay_2 (
    .s01(counter_4_q[1]), .s00(counter_4_q[0]), .g(m_7_segdisplay_2_g), .f(m_7_segdisplay_2_f),
    .e(m_7_segdisplay_2_e), .d(m_7_segdisplay_2_d), .c(m_7_segdisplay_2_c), .b(m_7_segdisplay_2_b),
    .a(m_7_segdisplay_2_a));
  _7_Segment_Display u_7_segment_display_3 (
    .g(m_7_segdisplay_1_g), .f(m_7_segdisplay_1_f), .a(m_7_segdisplay_1_a), .b(m_7_segdisplay_1_b),
    .e(m_7_segdisplay_1_e), .d(m_7_segdisplay_1_d), .c(m_7_segdisplay_1_c));  // open: dp
  _7_Segment_Display u_7_segment_display_4 (
    .g(m_7_segdisplay_2_g), .f(m_7_segdisplay_2_f), .a(m_7_segdisplay_2_a), .b(m_7_segdisplay_2_b),
    .e(m_7_segdisplay_2_e), .d(m_7_segdisplay_2_d), .c(m_7_segdisplay_2_c));  // open: dp
endmodule

module Tes_Timer (
  input  Back_To_0,
  input  Start_Condition,
  output out_3,
  output out_4,
  output out_5,
  output out_6,
  output out_7,
  output out_8,
  output out_9,
  output out_10,
  output out_11,
  output out_12,
  output out_13,
  output out_14,
  output out_15,
  output out_16,
  output out_17,
  output out_18,
  output out_19,
  output out_20,
  output out_21,
  output out_22,
  output out_23,
  output out_24,
  output out_25,
  output out_26,
  output out_27,
  output out_28,
  output out_29,
  output out_30,
  output out_31,
  output out_32
);

  wire and_1_out, and_3_out, and_4_out, and_5_out, and_6_out, and_8_out, and_9_out, clock_1_out,
       transistor_1_out;
  wire [3:0] counter_1_q, counter_2_q, counter_3_q, counter_4_q;

  Clock clock_1 (.out(clock_1_out));
  Counter #(.width(4), .max('h9)) counter_1 (
    .load(1'b1), .Q(counter_1_q), .clk(transistor_1_out), .clr(Back_To_0));  // open: D, count, carry
  Transistor transistor_1 (.in(clock_1_out), .out(transistor_1_out), .gate(out_31));
  Counter #(.width(4), .max('h5)) counter_2 (
    .load(1'b1), .Q(counter_2_q), .clk(and_1_out), .clr(Back_To_0));  // open: D, count, carry
  and and_1 (and_1_out, counter_1_q[3], counter_1_q[0], ~counter_1_q[2], ~counter_1_q[1]);  // AND_Gate
  and and_2 (out_31, ~Start_Condition, out_32);  // AND_Gate
  S__7_segDisplay s_7_segdisplay_1 (
    .s03(counter_1_q[3]), .s02(counter_1_q[2]), .s01(counter_1_q[1]), .s00(counter_1_q[0]), .g(out_3),
    .f(out_4), .e(out_5), .d(out_6), .c(out_7), .b(out_9), .a(out_11));
  S__7_segDisplay_2 s_7_segdisplay_2 (
    .s02(counter_2_q[2]), .s01(counter_2_q[1]), .s00(counter_2_q[0]), .g(out_17), .f(out_18), .e(out_20),
    .d(out_22), .c(out_24), .b(out_26), .a(out_28));
  and and_3 (and_3_out, ~counter_1_q[0], ~counter_1_q[1], ~counter_1_q[2], ~counter_1_q[3]);  // AND_Gate
  and and_4 (and_4_out, ~counter_2_q[0], ~counter_2_q[1], ~counter_2_q[2], ~counter_2_q[3]);  // AND_Gate
  and and_5 (and_5_out, ~counter_2_q[3], counter_2_q[2], ~counter_2_q[1], counter_2_q[0]);  // AND_Gate
  Counter #(.width(4), .max('h9)) counter_3 (
    .load(1'b1), .Q(counter_3_q), .clk(and_5_out), .clr(Back_To_0));  // open: D, count, carry
  and and_6 (and_6_out, ~counter_3_q[0], ~counter_3_q[1], ~counter_3_q[2], ~counter_3_q[3]);  // AND_Gate
  Counter #(.width(4), .max('h2)) counter_4 (
    .load(1'b1), .Q(counter_4_q), .clk(and_8_out), .clr(Back_To_0));  // open: D, count, carry
  and and_7 (out_32, and_4_out, and_3_out, and_6_out, and_9_out);
  and and_8 (and_8_out, counter_3_q[0], ~counter_3_q[1], ~counter_3_q[2], counter_3_q[3]);  // AND_Gate
  and and_9 (and_9_out, ~counter_4_q[0], ~counter_4_q[1], ~counter_4_q[2], ~counter_4_q[3]);  // AND_Gate
  M____7_segDisplay m_7_segdisplay_1 (
    .s03(counter_3_q[3]), .s02(counter_3_q[2]), .s01(counter_3_q[1]), .s00(counter_3_q[0]), .g(out_8),
    .f(out_10), .e(out_12), .d(out_13), .c(out_14), .b(out_15), .a(out_16));
  M_____7_segDisplay m_7_segdisplay_2 (
    .s01(counter_4_q[1]), .s00(counter_4_q[0]), .g(out_19), .f(out_21), .e(out_23), .d(out_25), .c(out_27),
    .b(out_29), .a(out_30));
endmodule
